// Logisim project Controller.circ as structural Verilog: 1 circuit, main circuit Controller
module Controller (
  input  [15:0] Inst,
  input  [3:0] FlagsIn,
  input  Clk,
  input  Reset,
  input  [31:0] R0,
  input  [31:0] R1,
  input  [31:0] R2,
  input  [31:0] R3,
  input  [31:0] R4,
  input  [31:0] R5,
  input  [31:0] R6,
  input  [31:0] R7,
  input  [31:0] RAM_Value,
  output Carry,
  output DP_Shift,
  output Imm32_Enable,
  output [4:0] Imm5,
  output [31:0] Imm32,
  output [3:0] ALU_Opcode,
  output [2:0] Rm,
  output [2:0] Rn,
  output [2:0] Rd,
  output [3:0] Flags,
  output [31:0] RAM_Addr,
  output Load,
  output Store,
  output [31:0] SP,
  output [15:0] PC
);

  wire and_1_out, comparator_1_eq, conditional_1_verified, load_address_1_imm32_enable, load_store_1_p20,
       not_1_out, opcode_decoder_1_conditional, opcode_decoder_1_data_processing,
       opcode_decoder_1_high_register_op, opcode_decoder_1_load_address, opcode_decoder_1_load_store,
       opcode_decoder_1_long_branch, opcode_decoder_1_shift, opcode_decoder_1_sp_address, or_3_out,
       shift_add_sub_mov_1_carry, shift_add_sub_mov_1_imm32_enable, sp_address_1_write_enable;
  wire [2:0] data_processing_1_rd, data_processing_1_rm, data_processing_1_rn, load_address_1_rd,
       load_store_1_p16, shift_add_sub_mov_1_rd, shift_add_sub_mov_1_rm, shift_add_sub_mov_1_rn;
  wire [3:0] data_processing_1_alu_opcode, data_processing_1_flags_update_mask, load_address_1_alu_opcode,
       or_1_out, shift_add_sub_mov_1_alu_opcode, shift_add_sub_mov_1_flags_update_mask;
  wire [10:0] conditional_1_offset, or_2_out, pull_resistor_1_node;
  wire [15:0] adder_1_out, adder_2_out, adder_3_out, bit_extender_1_out, Link_Register_q, multiplexer_1_out;
  wire [31:0] load_address_1_imm32, load_store_1_p21, shift_add_sub_mov_1_imm32,
       sp_address_1_new_stack_pointer;

  Register #(.width(32)) Stack_Pointer (
    .D(sp_address_1_new_stack_pointer), .en(sp_address_1_write_enable), .clk(Clk), .Q(SP), .clr(Reset));
  Opcode_Decoder opcode_decoder_1 (
    .Opcode(Inst[15:9]), .Shift(opcode_decoder_1_shift), .Data_Processing(opcode_decoder_1_data_processing),
    .Load_Store(opcode_decoder_1_load_store), .SP_Address(opcode_decoder_1_sp_address),
    .Conditional(opcode_decoder_1_conditional), .Load_Address(opcode_decoder_1_load_address),
    .Long_Branch(opcode_decoder_1_long_branch), .High_Register_Op(opcode_decoder_1_high_register_op));
  assign or_1_out = data_processing_1_flags_update_mask | shift_add_sub_mov_1_flags_update_mask;  // OR_Gate or_1, 4 bits wide
  Comparator #(.width(4)) comparator_1 (.a(Inst[9:6]), .b(4'b1101), .eq(comparator_1_eq));  // open: gt, lt
  Pull_Resistor pull_resistor_1 (.node(pull_resistor_1_node));
  assign pull_resistor_1_node = opcode_decoder_1_long_branch ? Inst[10:0] : 11'bz;  // Controlled_Buffer controlled_buffer_1
  and and_1 (and_1_out, comparator_1_eq, opcode_decoder_1_high_register_op);
  Conditional conditional_1 (
    .Offset(conditional_1_offset), .Verified(conditional_1_verified), .Instruction(Inst), .Z(Flags[2]),
    .C(Flags[1]), .N(Flags[3]), .V(Flags[0]), .Enable(opcode_decoder_1_conditional));
  Shift_Add_Sub_Mov shift_add_sub_mov_1 (
    .Flags_Update_Mask(shift_add_sub_mov_1_flags_update_mask), .Rm(shift_add_sub_mov_1_rm),
    .Rn(shift_add_sub_mov_1_rn), .Rd(shift_add_sub_mov_1_rd), .Imm5(Imm5), .Imm32(shift_add_sub_mov_1_imm32),
    .ALU_Opcode(shift_add_sub_mov_1_alu_opcode), .Carry(shift_add_sub_mov_1_carry),
    .Imm32_Enable(shift_add_sub_mov_1_imm32_enable), .Instruction(Inst), .Enable(opcode_decoder_1_shift));
  Data_Processing data_processing_1 (
    .Rn(data_processing_1_rn), .Rm(data_processing_1_rm), .ALU_Opcode(data_processing_1_alu_opcode),
    .Flags_Update_Mask(data_processing_1_flags_update_mask), .Rd(data_processing_1_rd), .Instruction(Inst),
    .Enable(opcode_decoder_1_data_processing));
  Flags_APSR flags_apsr_1 (.Update_Mask(or_1_out), .Flags_In(FlagsIn), .Clk(Clk), .Rst(Reset), .Flags_Out(Flags));
  // Load_Store load_store_1: pin names not known; wires that end beside it: Inst, opcode_decoder_1_load_store, SP, Clk, Reset, R0, R1, R2, R3, R4, R5, R6, R7, PC, RAM_Value, load_store_1_p16, RAM_Addr, Load, Store, load_store_1_p20, load_store_1_p21
  Load_Address load_address_1 (
    .Enable(opcode_decoder_1_load_address), .Instruction(Inst), .Program_Counter(PC), .Stack_Pointer(SP),
    .Imm32_Enable(load_address_1_imm32_enable), .Rd(load_address_1_rd),
    .ALU_Opcode(load_address_1_alu_opcode), .Imm32(load_address_1_imm32));
  assign bit_extender_1_out = {{5{or_2_out[10]}}, or_2_out};  // Bit_Extender bit_extender_1
  assign or_2_out = conditional_1_offset | pull_resistor_1_node;  // OR_Gate or_2, 11 bits wide
  or or_3 (or_3_out, conditional_1_verified, and_1_out, opcode_decoder_1_long_branch);
  Register #(.width(16)) Link_Register (
    .D(adder_1_out), .en(opcode_decoder_1_long_branch), .clk(Clk), .Q(Link_Register_q));  // open: clr
  Adder #(.width(16)) adder_1 (.a(16'h1), .b(PC), .out(adder_1_out));  // open: cin, cout
  SP_Address sp_address_1 (
    .New_Stack_Pointer(sp_address_1_new_stack_pointer), .Write_Enable(sp_address_1_write_enable),
    .Stack_Pointer(SP), .Instruction(Inst), .Enable(opcode_decoder_1_sp_address));
  Adder #(.width(16)) adder_2 (.a(16'h3), .b(bit_extender_1_out), .out(adder_2_out), .cin(1'b0));  // open: cout
  Adder #(.width(16)) adder_3 (.a(adder_2_out), .b(PC), .out(adder_3_out), .cin(1'b0));  // open: cout
  Multiplexer #(.width(16)) multiplexer_1 (
    .in0(adder_3_out), .in1(Link_Register_q), .out(multiplexer_1_out), .sel(and_1_out));
  and and_2 (DP_Shift, opcode_decoder_1_shift, ~opcode_decoder_1_data_processing);  // AND_Gate
  not not_1 (not_1_out, load_store_1_p20);
  Counter #(.max('hffff), .trigger("falling"), .width(16)) counter_1 (
    .clr(Reset), .load(or_3_out), .up(1'b1), .count(not_1_out), .clk(Clk), .D(multiplexer_1_out), .Q(PC));  // open: carry
  Multiplexer multiplexer_2 (.in0(Flags[1]), .in1(shift_add_sub_mov_1_carry), .out(Carry), .sel(DP_Shift));
  or or_4 (Imm32_Enable, shift_add_sub_mov_1_imm32_enable, load_address_1_imm32_enable);
  assign Imm32 = shift_add_sub_mov_1_imm32 | load_store_1_p21 | load_address_1_imm32;  // OR_Gate or_5, 32 bits wide
  assign ALU_Opcode = shift_add_sub_mov_1_alu_opcode | data_processing_1_alu_opcode | load_address_1_alu_opcode;  // OR_Gate or_6, 4 bits wide
  assign Rm = shift_add_sub_mov_1_rm | data_processing_1_rm | load_store_1_p16;  // OR_Gate or_7, 3 bits wide
  assign Rn = shift_add_sub_mov_1_rn | data_processing_1_rn | load_store_1_p16;  // OR_Gate or_8, 3 bits wide
  assign Rd = shift_add_sub_mov_1_rd | data_processing_1_rd | load_store_1_p16 | load_address_1_rd;  // OR_Gate or_9, 3 bits wide

  // Notes on the sheet:
  //   Extract carry
  //   Extract Opcode
  //   IF Reg_Imm=1 THEN use shift value from register ELSE use shift value from Imm5
  //   Buffer flags for next instruction
  //   Add 3 to offset because ARM pre-increments PC
  //   and does an additional prefetch operation
endmodule
