// Logisim project Machine.circ as structural Verilog: 2 circuits, main circuit main
module main (
);

  wire Clk_Button_out, Rst_Button_out;
  wire [7:0] RAM_Addr, ROM_Addr;
  wire [15:0] ROM_1_data_2;
  wire [31:0] CPU_1_r0, CPU_1_r1, CPU_1_r2, CPU_1_r3, CPU_1_r4, CPU_1_r5, CPU_1_r6, CPU_1_r7, rom_1_data;
  wire [31:8] CPU_1_ram_addr;

  // Probe on RAM_Addr
  ROM #(.dataWidth(32)) rom_1 (.addr(RAM_Addr), .data(rom_1_data));
  Button Clk_Button (.out(Clk_Button_out));
  Button Rst_Button (.out(Rst_Button_out));
  // Probe on ROM_Addr
  ROM #(.dataWidth(16)) ROM_1_dup2 (.addr(ROM_Addr), .data(ROM_1_data_2));
  // Probe on CPU_1_r3
  // Probe on CPU_1_r2
  // Probe on CPU_1_r1
  // Probe on CPU_1_r0
  // Probe on CPU_1_r7
  // Probe on CPU_1_r6
  // Probe on CPU_1_r5
  // Probe on CPU_1_r4
  CPU CPU_1 (
    .Clk(Clk_Button_out), .ROM_Addr(ROM_Addr), .ROM_In(ROM_1_data_2), .RAM_In(rom_1_data),
    .RAM_Addr({CPU_1_ram_addr, RAM_Addr}), .Rst(Rst_Button_out), .R0(CPU_1_r0), .R1(CPU_1_r1), .R2(CPU_1_r2),
    .R3(CPU_1_r3), .R4(CPU_1_r4), .R5(CPU_1_r5), .R6(CPU_1_r6), .R7(CPU_1_r7));  // open: RAM_Out

  // Notes on the sheet:
  //   contents of rom_1 (hex, n*v repeats v):
  //   1 3 2 4
  //   contents of ROM_1 (hex, n*v repeats v):
  //   9800 9900 1a08 d002 9a02 9801 c9 4308
  //   Use only 8 bit adresses
endmodule

module CPU (
  input  [31:0] RAM_In,
  input  [15:0] ROM_In,
  input  Clk,
  input  Rst,
  output [7:0] ROM_Addr,
  output [31:0] RAM_Addr,
  output [31:0] RAM_Out,
  output [31:0] R3,
  output [31:0] R7,
  output [31:0] R2,
  output [31:0] R6,
  output [31:0] R1,
  output [31:0] R5,
  output [31:0] R0,
  output [31:0] R4
);

  wire controller_1_carry, controller_1_dp_shift, controller_1_load, controller_1_move;
  wire [2:0] controller_1_rd, controller_1_rm, controller_1_rn;
  wire [3:0] ALU_1_flags, controller_1_alu_opcode;
  wire [4:0] controller_1_imm5, multiplexer_3_out;
  wire [7:0] controller_1_imm8;
  wire [31:0] ALU_1_s, bit_extender_1_out, multiplexer_1_out, multiplexer_2_out, Regs_1_p15, undriven;

  Controller controller_1 (
    .Rm(controller_1_rm), .Inst(ROM_In), .Move(controller_1_move), .PC(ROM_Addr), .Rn(controller_1_rn),
    .Imm5(controller_1_imm5), .ALU_Opcode(controller_1_alu_opcode), .Flags(ALU_1_flags),
    .Imm8(controller_1_imm8), .Rd(controller_1_rd), .DP_Shift(controller_1_dp_shift),
    .Carry(controller_1_carry), .RAM_Addr(RAM_Addr), .Load(controller_1_load), .Clk(Clk), .Reset(Rst));  // open: Store
  Multiplexer #(.width(32), .enable("false")) multiplexer_1 (
    .in0(undriven), .in1(RAM_In), .out(multiplexer_1_out), .sel(controller_1_load));
  assign bit_extender_1_out = {{24{controller_1_imm8[7]}}, controller_1_imm8};  // Bit_Extender bit_extender_1
  Multiplexer #(.width(32), .enable("false")) multiplexer_2 (
    .in0(multiplexer_1_out), .in1(bit_extender_1_out), .out(multiplexer_2_out), .sel(controller_1_move));
  // BancRegistre Regs_1: pin names not known; wires that end beside it: multiplexer_2_out, controller_1_rd, Clk, R0, Rst, R1, R2, R3, R4, controller_1_rm, R5, R6, controller_1_rn, R7, Regs_1_p15, RAM_Out
  Multiplexer #(.width(5), .enable("false")) multiplexer_3 (
    .in0(RAM_Out[4:0]), .in1(controller_1_imm5), .out(multiplexer_3_out), .sel(controller_1_dp_shift));
  ALU ALU_1 (
    .S(ALU_1_s), .Flags(ALU_1_flags), .A(RAM_Out), .B(Regs_1_p15), .Shift(multiplexer_3_out),
    .CarryIn(controller_1_carry), .Codop(controller_1_alu_opcode));

  // Notes on the sheet:
  //   RAM/ALU Input selector
  //   Use data from register or immediate for shift
  //   Imm8 input for Move
endmodule
