// Logisim project Machine_Logisim3.circ as structural Verilog: 4 circuits, main circuit main
module main (
);

  wire and_1_out, and_2_out, and_3_out, and_4_out, and_5_out, and_6_out, BREAK, Clk, Clk_Button2,
       Clk_Button_out, clock_1_out, CONTINUE, d_ff_3_qn, decoder_1_out0, decoder_1_out1, decoder_1_out2,
       decoder_1_out3, decoder_1_out4, decoder_1_out5, decoder_1_out6, KEYB_Eof, KEYB_Read, KEYB_ReadEn,
       midi2freq_1_enable, MMIO_En, or_1_out, or_4_out, Reset, RNG_Read, Rst_Button_out, RST_Signal, Store,
       TTY_Upd;
  wire [3:0] binary_to_bcd_converter_1_p2, binary_to_bcd_converter_1_p3, binary_to_bcd_converter_1_p4,
       binary_to_bcd_converter_1_p5, MMIO_Addr;
  wire [4:0] JOY_X, JOY_Y;
  wire [6:0] KEYB_Char, TTY_Char;
  wire [7:0] register_6_q;
  wire [7:4] RAM_Addr;
  wire [13:0] midi2freq_1_freq;
  wire [15:0] multiplier_1_out, ROM_Addr, ROMa_data;
  wire [31:0] bcd8digits_1_bcd, CPU_1_r0, CPU_1_r1, CPU_1_r4, CPU_1_r5, CPU_1_r6, CPU_1_r7, Dip1, Dip2, Dip3,
       divider_1_out, divider_1_rem, MMIO_Out, multiplexer_1_out, R2, R3, RAM_Out, RAMa_dout, random_1_out,
       register_3_q, Res, Screen;
  wire [31:1] undriven_2;
  wire [31:5] undriven_4, undriven_5;
  wire [31:7] undriven, undriven_3;
  wire [31:9] CPU_1_ram_addr;

  Decoder #(.select(4)) decoder_1 (
    .out0(decoder_1_out0), .out1(decoder_1_out1), .out2(decoder_1_out2), .out3(decoder_1_out3),
    .out4(decoder_1_out4), .out5(decoder_1_out5), .out6(decoder_1_out6), .sel(MMIO_Addr), .en(and_1_out));  // open: out7, out8, out9, out10, out11, out12, out13, out14, out15
  DipSwitch dipswitch_1 (
    .sw1(Dip1[7]), .sw2(Dip1[6]), .sw3(Dip1[5]), .sw4(Dip1[4]), .sw5(Dip1[3]), .sw6(Dip1[2]), .sw7(Dip1[1]),
    .sw8(Dip1[0]));
  and and_1 (and_1_out, MMIO_En, Store);
  // Probe on MMIO_Addr
  // Probe on Dip1[7:0]
  DipSwitch dipswitch_2 (
    .sw1(Dip2[7]), .sw2(Dip2[6]), .sw3(Dip2[5]), .sw4(Dip2[4]), .sw5(Dip2[3]), .sw6(Dip2[2]), .sw7(Dip2[1]),
    .sw8(Dip2[0]));
  Keyboard keyboard_1 (.clk(Clk), .re(KEYB_ReadEn), .clr(Reset), .avail(KEYB_Eof), .data(KEYB_Char));
  RAM #(.dataWidth(32)) RAMa (
    .addr({RAM_Addr, MMIO_Addr}), .we(and_2_out), .oe(1'b1), .clk(Clk), .din(RAM_Out), .dout(RAMa_dout));
  and and_2 (and_2_out, ~MMIO_En, Store);  // AND_Gate
  // Probe on Dip2[7:0]
  // Probe on {MMIO_En, RAM_Addr, MMIO_Addr}
  Register #(.trigger("falling"), .width(7)) register_1 (
    .D(RAM_Out[6:0]), .en(decoder_1_out0), .clk(Clk), .Q(TTY_Char), .clr(Reset));
  Register #(.width(32)) register_2 (.D(RAM_Out), .en(decoder_1_out1), .clk(Clk), .Q(Res), .clr(Reset));
  Register #(.width(32)) register_3 (.D(RAM_Out), .en(decoder_1_out2), .clk(Clk), .Q(register_3_q), .clr(Reset));
  Register #(.width(1)) register_4 (.D(RAM_Out[0]), .en(decoder_1_out4), .clk(Clk), .Q(RST_Signal), .clr(Reset));
  Register #(.width(1)) register_5 (.D(RAM_Out[0]), .en(decoder_1_out5), .clk(Clk), .Q(BREAK), .clr(or_1_out));
  or or_1 (or_1_out, Reset, CONTINUE);
  Register register_6 (.D(RAM_Out[7:0]), .en(decoder_1_out6), .clk(Clk), .Q(register_6_q), .clr(Reset));
  // Probe on Dip3[7:0]
  DipSwitch dipswitch_3 (
    .sw1(Dip3[7]), .sw2(Dip3[6]), .sw3(Dip3[5]), .sw4(Dip3[4]), .sw5(Dip3[3]), .sw6(Dip3[2]), .sw7(Dip3[1]),
    .sw8(Dip3[0]));
  D_Flip_Flop d_ff_1 (.D(decoder_1_out0), .clk(Clk), .Q(TTY_Upd));  // open: Qn, preset, reset
  Register #(.width(32)) register_7 (.D(register_3_q), .en(and_3_out), .clk(Clk), .Q(Screen), .clr(Reset));
  and and_3 (and_3_out, RAM_Out[0], decoder_1_out3);
  Joystick #(.bits(5)) joystick_1 (.x(JOY_X), .y(JOY_Y));
  Clock clock_1 (.out(clock_1_out));
  MIDI2Freq midi2freq_1 (.Enable(midi2freq_1_enable), .Freq(midi2freq_1_freq), .MIDI(register_6_q));
  DotMatrix #(.inputtype("row"), .matrixcols(8), .matrixrows(4)) dotmatrix_1 (
    .row0(Screen[7:0]), .row1(Screen[15:8]), .row2(Screen[23:16]), .row3(Screen[31:24]));
  or or_2 (Clk, and_4_out, Clk_Button_out, Clk_Button2);
  and and_4 (and_4_out, clock_1_out, ~BREAK);  // AND_Gate
  Button Clk_Button (.out(Clk_Button_out));
  Button Rst_Button (.out(Rst_Button_out));
  ROM #(.addrWidth(16), .dataWidth(16)) ROMa (.addr(ROM_Addr), .data(ROMa_data));
  // Buzzer buzzer_1: pin names not known; wires that end beside it: midi2freq_1_freq, midi2freq_1_enable, {7{1'b1}}
  or or_3 (Reset, Rst_Button_out, RST_Signal);
  // Probe on RAMa_dout
  D_Flip_Flop d_ff_2 (.D(KEYB_Read), .clk(Clk), .Q(KEYB_ReadEn), .reset(or_4_out));  // open: Qn, preset
  or or_4 (or_4_out, ~KEYB_Read, Reset);  // OR_Gate
  Hex_Digit_Display hex_digit_display_1 (.value(Res[15:12]));  // open: dp
  D_Flip_Flop #(.trigger("falling")) d_ff_3 (.D(1'b0), .clk(Clk), .Qn(d_ff_3_qn), .preset(Reset));  // open: Q, reset
  DotMatrix #(.inputtype("row"), .matrixcols(32), .matrixrows(1)) dotmatrix_2 (.row0(Res));
  Hex_Digit_Display hex_digit_display_2 (.value(Res[11:8]));  // open: dp
  Hex_Digit_Display hex_digit_display_3 (.value(Res[7:4]));  // open: dp
  Multiplexer #(.enable("false"), .width(32)) multiplexer_1 (
    .in0(RAMa_dout), .in1(MMIO_Out), .out(multiplexer_1_out), .sel(MMIO_En));
  // Probe on multiplexer_1_out
  Button button_1 (.out(CONTINUE));
  Hex_Digit_Display hex_digit_display_4 (.value(Res[3:0]));  // open: dp
  // Probe on CPU_1_r1
  // Probe on CPU_1_r0
  and and_5 (and_5_out, Clk, d_ff_3_qn);
  Random #(.width(32)) random_1 (.next(RNG_Read), .clk(Clk), .out(random_1_out));  // open: clr
  Hex_Digit_Display hex_digit_display_5 (.value(binary_to_bcd_converter_1_p2));  // open: dp
  // Binary_to_BCD_converter #(.binvalue(13)) binary_to_bcd_converter_1: pin names not known; wires that end beside it: Res[12:0], binary_to_bcd_converter_1_p2, binary_to_bcd_converter_1_p3, binary_to_bcd_converter_1_p4, binary_to_bcd_converter_1_p5
  // Probe on R3
  // Probe on R2
  // Probe on CPU_1_r5
  // Probe on CPU_1_r4
  BCD8digits bcd8digits_1 (.BCD(bcd8digits_1_bcd), .Number(Res));
  Divider #(.width(32)) divider_1 (.a(R2), .b(R3), .out(divider_1_out), .rem(divider_1_rem));  // open: upper
  Button button_2 (.out(Clk_Button2));
  // Probe on Res
  Hex_Digit_Display hex_digit_display_6 (.value(binary_to_bcd_converter_1_p3));  // open: dp
  Hex_Digit_Display hex_digit_display_7 (.value(binary_to_bcd_converter_1_p4));  // open: dp
  // Probe on CPU_1_r7
  // Probe on CPU_1_r6
  CPU CPU_1 (
    .ROM_Addr(ROM_Addr), .RAM_Addr({CPU_1_ram_addr, MMIO_En, RAM_Addr, MMIO_Addr}), .Store(Store),
    .RAM_Out(RAM_Out), .R0(CPU_1_r0), .R1(CPU_1_r1), .R2(R2), .R3(R3), .R4(CPU_1_r4), .R5(CPU_1_r5),
    .R6(CPU_1_r6), .R7(CPU_1_r7), .ROM_In(ROMa_data), .Clk(and_5_out), .Reset(Reset),
    .RAM_In(multiplexer_1_out));
  Hex_Digit_Display hex_digit_display_8 (.value(binary_to_bcd_converter_1_p5));  // open: dp
  // Probe on RAM_Out
  Multiplexer #(.enable("false"), .select(4), .width(32)) multiplexer_2 (
    .in0({undriven, TTY_Char}), .in1(Res), .in2(register_3_q), .in3(Dip1), .in4(Dip2), .in5(Dip3),
    .in6({undriven_2, KEYB_Eof}), .in7({undriven_3, KEYB_Char}), .in8({undriven_4, JOY_X}),
    .in9({undriven_5, JOY_Y}), .in10(random_1_out), .in11(bcd8digits_1_bcd), .in12(divider_1_out),
    .in13(divider_1_rem), .out(MMIO_Out), .sel(MMIO_Addr));  // open: in14, in15
  TTY tty_1 (.data(TTY_Char), .clk(Clk), .we(TTY_Upd), .clr(Reset));
  Multiplier #(.width(16)) multiplier_1 (.a(16'h2), .b(ROM_Addr), .out(multiplier_1_out));  // open: cin, cout
  // Probe on {MMIO_En, RAM_Addr, MMIO_Addr}
  and and_6 (and_6_out, ~Store, MMIO_En);  // AND_Gate
  Decoder #(.select(4)) decoder_2 (
    .out7(KEYB_Read), .out10(RNG_Read), .sel(MMIO_Addr), .en(and_6_out));  // open: out0, out1, out2, out3, out4, out5, out6, out8, out9, out11, out12, out13, out14, out15
  Pull_Resistor pull_resistor_1 (.node(MMIO_Out));
  // Probe on multiplier_1_out

  // Other names for the same wires on the sheet: RAM_Addr (some bits) = {MMIO_En, MMIO_Addr}

  // Notes on the sheet:
  //   contents of ROMa (hex, n*v repeats v):
  //   b090 b0ff b0f1 2050 9000 2041 9000 2052 9000 204d 9000 2045 9000 2053 9000 2041 9000 204e 9000 2021
  //   9000 e7fd 9006 20c5 9006 20bc 9006 20c0 9006 20c5 9006 20c7 9006 20c7 9006 20c7 9006 20c0 9006 20c4
  //   9006 20c7 9006 20c8
endmodule

module CPU (
  input  [31:0] RAM_In,
  input  [15:0] ROM_In,
  input  Clk,
  input  Reset,
  output [31:0] R3,
  output [31:0] R7,
  output [31:0] R2,
  output [31:0] R6,
  output [31:0] R1,
  output [31:0] R5,
  output [31:0] R0,
  output [31:0] R4,
  output [15:0] ROM_Addr,
  output [31:0] RAM_Addr,
  output Store,
  output [31:0] RAM_Out
);

  wire and_1_out, Controller_1_carry, Controller_1_dp_shift, Controller_1_imm32_enable, Controller_1_load;
  wire [2:0] Controller_1_rd, Controller_1_rm, Controller_1_rn;
  wire [3:0] ALU_1_flags, Controller_1_alu_opcode;
  wire [4:0] Controller_1_imm5, multiplexer_3_out;
  wire [31:0] ALU_1_s, Controller_1_imm32, multiplexer_1_out, multiplexer_2_out, Regs_1_bout;

  // Probe on Controller_1_rd
  and and_1 (and_1_out, Clk, ~Store);  // AND_Gate
  // Probe on multiplexer_1_out
  Multiplexer #(.enable("false"), .width(32)) multiplexer_1 (
    .in0(ALU_1_s), .in1(RAM_In), .out(multiplexer_1_out), .sel(Controller_1_load));
  Controller Controller_1 (
    .ALU_Opcode(Controller_1_alu_opcode), .Imm32_Enable(Controller_1_imm32_enable), .Rd(Controller_1_rd),
    .Imm5(Controller_1_imm5), .Inst(ROM_In), .PC(ROM_Addr), .Flags(ALU_1_flags), .Imm32(Controller_1_imm32),
    .Rn(Controller_1_rn), .Rm(Controller_1_rm), .DP_Shift(Controller_1_dp_shift), .Carry(Controller_1_carry),
    .RAM_Addr(RAM_Addr), .Load(Controller_1_load), .Store(Store), .Clk(Clk), .Reset(Reset));
  // Probe on Controller_1_rm
  // Probe on Controller_1_rn
  BancRegistre Regs_1 (
    .Clk(and_1_out), .Reset(Reset), .DataIn(multiplexer_1_out), .RegB(Controller_1_rn), .AOut(RAM_Out),
    .R0(R0), .R1(R1), .R2(R2), .R3(R3), .R4(R4), .R5(R5), .R6(R6), .R7(R7), .RegA(Controller_1_rm),
    .RegDest(Controller_1_rd), .BOut(Regs_1_bout));
  // Probe on RAM_Out
  Multiplexer #(.enable("false"), .width(32)) multiplexer_2 (
    .in0(RAM_Out), .in1(Controller_1_imm32), .out(multiplexer_2_out), .sel(Controller_1_imm32_enable));
  Multiplexer #(.enable("false"), .width(5)) multiplexer_3 (
    .in0(RAM_Out[4:0]), .in1(Controller_1_imm5), .out(multiplexer_3_out), .sel(Controller_1_dp_shift));
  // Probe on Regs_1_bout
  ALU ALU_1 (
    .S(ALU_1_s), .Flags(ALU_1_flags), .A(multiplexer_2_out), .B(Regs_1_bout), .Shift(multiplexer_3_out),
    .CarryIn(Controller_1_carry), .Codop(Controller_1_alu_opcode));
  // Probe on Controller_1_alu_opcode
  // Probe on ALU_1_s
endmodule

module BCD8digits (
  input  [31:0] Number,
  output [31:0] BCD
);

  wire [31:0] divider_1_out, divider_2_out, divider_3_out, divider_4_out, divider_5_out, divider_6_out,
       divider_7_out;
  wire [31:4] divider_1_rem, divider_2_rem, divider_3_rem, divider_4_rem, divider_5_rem, divider_6_rem,
       divider_7_rem, divider_8_rem;

  Divider #(.width(32)) divider_1 (
    .a(Number), .b(32'ha), .out(divider_1_out), .rem({divider_1_rem, BCD[31:28]}));  // open: upper
  Divider #(.width(32)) divider_2 (
    .a(divider_1_out), .b(32'ha), .out(divider_2_out), .rem({divider_2_rem, BCD[27:24]}));  // open: upper
  Divider #(.width(32)) divider_3 (
    .a(divider_2_out), .b(32'ha), .out(divider_3_out), .rem({divider_3_rem, BCD[23:20]}));  // open: upper
  Divider #(.width(32)) divider_4 (
    .a(divider_3_out), .b(32'ha), .out(divider_4_out), .rem({divider_4_rem, BCD[19:16]}));  // open: upper
  Divider #(.width(32)) divider_5 (
    .a(divider_4_out), .b(32'ha), .out(divider_5_out), .rem({divider_5_rem, BCD[15:12]}));  // open: upper
  Divider #(.width(32)) divider_6 (
    .a(divider_5_out), .b(32'ha), .out(divider_6_out), .rem({divider_6_rem, BCD[11:8]}));  // open: upper
  Divider #(.width(32)) divider_7 (
    .a(divider_6_out), .b(32'ha), .out(divider_7_out), .rem({divider_7_rem, BCD[7:4]}));  // open: upper
  Divider #(.width(32)) divider_8 (.a(divider_7_out), .b(32'ha), .rem({divider_8_rem, BCD[3:0]}));  // open: out, upper
  // Probe on BCD
endmodule

module MIDI2Freq (
  input  [7:0] MIDI,
  output Enable,
  output [13:0] Freq
);

  ROM #(.addrWidth(7), .dataWidth(14)) rom_1 (.addr(MIDI[6:0]), .data(Freq));

  assign Enable = MIDI[7];

  // Notes on the sheet:
  //   contents of rom_1 (hex, n*v repeats v):
  //   8 9 9 a a b c c d e f f 10 11 12 13 15 16 17 18 1a 1c 1d 1f 21 23 25 27 29 2c 2e 31 34 37 3a 3e 41
  //   45 49 4e 52 57 5c 62 68 6e 75 7b 83 8b 93 9c a5 af b9 c4 d0 dc e9 f7 106 115 126 137 14a 15d 172 188
  //   19f 1b8 1d2 1ee 20b 22a 24b 26e 293 2ba 2e4 310 33f 370 3a4 3dc 417 455 497 4dd 527 575 5c8 620 67d
  //   6e0 749 7b8 82d 8a9 92d 9b9 a4d aea b90 c40 cfa dc0 e91 f6f 105a 1153 125b 1372 149a 15d4 1720 1880
  //   19f5 1b80 1d23 1ede 20b4 22a6 24b5 26e4 2934 2ba7 2e40 3100
endmodule
